# Fritzing sketch co_mecanum (saved by Fritzing 0.9.3b)

parts:
  U2 = NodeMCU V1.0
  VCC2 = Battery  # not connected
  L298N2 = L298N DC motor driver
  M1 = DC Motor  # not connected
  M2 = DC Motor  # not connected
  M3 = DC Motor  # not connected
  M4 = DC Motor  # not connected

nets:
  N1: U2.D1, U2.D5, U2.D6, U2.D7, U2.D8, L298N2.5V#9, L298N2.5V#10, L298N2.ENA, L298N2.ENB, L298N2.IN1, L298N2.IN2
  N2: U2.D3, L298N2.IN4
  N3: U2.D4, L298N2.IN3
  N4: U2.Vin, L298N2.5V#7
  GND: U2.GND, L298N2.GND

custom parts:
  NodeMCU V1.0: ESP8266 based NodeMCU V1.0
  L298N DC motor driver: 2x DC motor driver with 78M05 positive voltage regulator (7..35 V) L298N: max 46 V, 2 A Set 5 V Enable jumper to enable 5 V regultor (needed for the L298N) and +5 V output at screw terminal or supply external +5 V at screw terminal Set ENA and/or ENB to +5 V to enable motor permanently or supply ENA and/or ENB with PWM signal IN1 and IN2 set rotation directory for motor A (OUT1/OUT2) IN2 and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
