# Fritzing sketch ko_mecanum (saved by Fritzing 0.9.3b)

parts:
  U1 = NodeMCU V1.0
  VCC1 = Battery
  L298N1 = L298N DC motor driver
  M1 = DC Motor  # not connected
  M2 = DC Motor  # not connected
  M3 = DC Motor  # not connected
  M4 = DC Motor  # not connected

nets:
  N1: U1.D1, U1.D5, U1.D6, U1.D7, U1.D8, L298N1.ENA, L298N1.ENB, L298N1.IN1, L298N1.IN2
  N2: U1.D3, L298N1.IN4
  N3: U1.D4, L298N1.IN3
  VIN: U1.Vin, L298N1.5V
  GND: U1.GND, VCC1.-, L298N1.GND

custom parts:
  NodeMCU V1.0: ESP8266 based NodeMCU V1.0
  L298N DC motor driver: 2x DC motor driver with 78M05 positive voltage regulator (7..35 V) L298N: max 46 V, 2 A Set 5 V Enable jumper to enable 5 V regultor (needed for the L298N) and +5 V output at screw terminal or supply external +5 V at screw terminal Set ENA and/or ENB to +5 V to enable motor permanently or supply ENA and/or ENB with PWM signal IN1 and IN2 set rotation directory for motor A (OUT1/OUT2) IN2 and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
